// Logisim project 3-8decoder.circ as structural Verilog: 2 circuits, main circuit main
module main (
  input  D0,
  input  D1,
  input  D2,
  input  G1,
  input  G2,
  output Y0,
  output Y1,
  output Y2,
  output Y3,
  output Y4,
  output Y5,
  output Y6,
  output Y7
);

  wire and_1_out, not_1_out, not_2_out, not_3_out, not_4_out;

  not not_1 (not_1_out, G2);
  not not_2 (not_2_out, D0);
  not not_3 (not_3_out, D1);
  not not_4 (not_4_out, D2);
  and and_1 (and_1_out, G1, not_1_out);
  nand nand_1 (Y0, not_2_out, not_3_out, not_4_out, and_1_out);
  nand nand_2 (Y1, D0, not_3_out, not_4_out, and_1_out);
  nand nand_3 (Y2, not_2_out, D1, not_4_out, and_1_out);
  nand nand_4 (Y3, D0, D1, not_4_out, and_1_out);
  nand nand_5 (Y4, not_2_out, not_3_out, D2, and_1_out);
  nand nand_6 (Y5, D0, not_3_out, D2, and_1_out);
  nand nand_7 (Y6, not_2_out, D1, D2, and_1_out);
  nand nand_8 (Y7, D0, D1, D2, and_1_out);
endmodule

module _3_8decoder (
  input  D2,
  input  D1,
  input  D0,
  input  G1,
  input  G2,
  output Y2,
  output Y1,
  output Y0,
  output Y3,
  output Y4,
  output Y5,
  output Y6,
  output Y7
);

  wire not_1_out, not_2_out, not_3_out, not_4_out, not_5_out, not_6_out, not_7_out, not_8_out, not_9_out,
       not_10_out, not_11_out, not_12_out, not_13_out, not_14_out, not_15_out, not_16_out, not_17_out,
       not_18_out, not_19_out, not_20_out;

  not not_1 (not_1_out, D2);
  not not_2 (not_2_out, D2);
  not not_3 (not_3_out, G2);
  not not_4 (not_4_out, D2);
  not not_5 (not_5_out, G1);
  not not_6 (not_6_out, D2);
  not not_7 (not_7_out, G1);
  not not_8 (not_8_out, G2);
  not not_9 (not_9_out, D2);
  not not_10 (not_10_out, D0);
  not not_11 (not_11_out, D2);
  not not_12 (not_12_out, D0);
  not not_13 (not_13_out, G2);
  not not_14 (not_14_out, D2);
  not not_15 (not_15_out, D0);
  not not_16 (not_16_out, G1);
  not not_17 (not_17_out, D2);
  not not_18 (not_18_out, D0);
  not not_19 (not_19_out, G1);
  not not_20 (not_20_out, G2);
  or or_1 (Y2, not_1_out, G2, G1, D0, D1);
  or or_2 (Y1, not_2_out, not_3_out, G1, D0, D1);
  or or_3 (Y0, not_4_out, not_5_out, G2, D0, D1);
  or or_4 (Y3, not_6_out, not_7_out, not_8_out, D0, D1);
  or or_5 (Y4, not_9_out, not_10_out, G2, G1, D1);
  or or_6 (Y5, not_11_out, not_12_out, not_13_out, G1, D1);
  or or_7 (Y6, not_14_out, not_15_out, not_16_out, G2, D1);
  or or_8 (Y7, not_17_out, not_18_out, not_19_out, not_20_out, D1);
endmodule
