// Logisim project DataCompare4.circ as structural Verilog: 1 circuit, main circuit main
module main (
  input  B3,
  input  A3,
  input  B2,
  input  A2,
  input  B1,
  input  A1,
  input  B0,
  input  A0
);

  wire and_1_out, and_2_out, and_3_out, and_4_out, and_5_out, and_6_out, and_7_out, and_8_out, not_1_out,
       not_2_out, not_3_out, not_4_out, not_5_out, not_6_out, not_7_out, not_8_out, or_1_out, or_2_out,
       or_3_out, or_4_out;

  not not_1 (not_1_out, B3);
  not not_2 (not_2_out, A3);
  not not_3 (not_3_out, B2);
  not not_4 (not_4_out, A2);
  not not_5 (not_5_out, B1);
  not not_6 (not_6_out, A1);
  not not_7 (not_7_out, B0);
  not not_8 (not_8_out, A0);
  and and_1 (and_1_out, not_1_out, A3);
  and and_2 (and_2_out, B3, not_2_out);
  and and_3 (and_3_out, not_3_out, A2);
  and and_4 (and_4_out, B2, not_4_out);
  and and_5 (and_5_out, not_5_out, A1);
  and and_6 (and_6_out, B1, not_6_out);
  and and_7 (and_7_out, not_7_out, A0);
  and and_8 (and_8_out, B0, not_8_out);
  or or_1 (or_1_out, and_1_out, and_2_out);
  or or_2 (or_2_out, and_3_out, and_4_out);
  or or_3 (or_3_out, and_5_out, and_6_out);
  or or_4 (or_4_out, and_7_out, and_8_out);
  // AND_Gate and_9 has open pins: in0=or_1_out, in1=and_3_out, out=open
  // AND_Gate and_10 has open pins: in0=and_4_out, in1=or_1_out, out=open
  // AND_Gate and_11 has open pins: in0=or_1_out, in1=or_2_out, in2=and_5_out, out=open
  // AND_Gate and_12 has open pins: in0=and_6_out, in1=or_2_out, in2=or_1_out, out=open
  // AND_Gate and_13 has open pins: in0=or_1_out, in1=or_2_out, in2=or_3_out, in3=and_7_out, out=open
  // AND_Gate and_14 has open pins: in0=and_8_out, in1=or_3_out, in2=or_2_out, in3=or_1_out, out=open
endmodule
