// Logisim project barrelshifter.circ as structural Verilog: 1 circuit, main circuit main
module main (
  input  _0,
  input  a0,
  input  a1,
  input  a2,
  input  a3,
  input  a4,
  input  a5,
  input  a6,
  input  a7,
  input  aluc0,
  input  aluc1,
  input  en,
  input  in_13,
  input  in_14,
  input  in_15,
  output out_16,
  output out_17,
  output out_18,
  output out_19,
  output out_20,
  output out_21,
  output out_22,
  output out_23
);

  wire and_1_out, multiplexer_1_out, multiplexer_2_out, multiplexer_3_out, multiplexer_4_out,
       multiplexer_5_out, multiplexer_6_out, multiplexer_7_out, multiplexer_8_out, multiplexer_9_out,
       multiplexer_10_out, multiplexer_11_out, multiplexer_12_out, multiplexer_13_out, multiplexer_14_out,
       multiplexer_15_out, multiplexer_16_out, multiplexer_17_out, multiplexer_18_out, multiplexer_19_out,
       multiplexer_20_out, multiplexer_21_out, multiplexer_22_out, multiplexer_23_out, multiplexer_24_out,
       multiplexer_25_out, multiplexer_26_out, multiplexer_27_out, multiplexer_28_out, multiplexer_29_out,
       multiplexer_30_out, multiplexer_31_out, multiplexer_32_out, multiplexer_33_out, multiplexer_34_out,
       multiplexer_35_out, multiplexer_36_out, multiplexer_37_out, multiplexer_38_out, multiplexer_39_out,
       multiplexer_40_out, not_1_out, not_2_out;

  not not_1 (not_1_out, aluc0);
  not not_2 (not_2_out, aluc1);
  and and_1 (and_1_out, a7, not_1_out);
  Multiplexer multiplexer_1 (.in0(_0), .in1(a1), .out(multiplexer_1_out), .sel(not_2_out), .en(en));
  Multiplexer multiplexer_2 (.in0(a0), .in1(a2), .out(multiplexer_2_out), .sel(not_2_out), .en(en));
  Multiplexer multiplexer_3 (.in0(a1), .in1(a3), .out(multiplexer_3_out), .sel(not_2_out), .en(en));
  Multiplexer multiplexer_4 (.in0(a2), .in1(a4), .out(multiplexer_4_out), .sel(not_2_out), .en(en));
  Multiplexer multiplexer_5 (.in0(a3), .in1(a5), .out(multiplexer_5_out), .sel(not_2_out), .en(en));
  Multiplexer multiplexer_6 (.in0(a4), .in1(a6), .out(multiplexer_6_out), .sel(not_2_out), .en(en));
  Multiplexer multiplexer_7 (.in0(a5), .in1(a7), .out(multiplexer_7_out), .sel(not_2_out), .en(en));
  Multiplexer multiplexer_8 (.in0(a6), .in1(and_1_out), .out(multiplexer_8_out), .sel(not_2_out), .en(en));
  Multiplexer multiplexer_9 (.in0(a0), .in1(multiplexer_1_out), .out(multiplexer_9_out), .sel(in_14), .en(en));
  Multiplexer multiplexer_10 (.in0(a1), .in1(multiplexer_2_out), .out(multiplexer_10_out), .sel(in_14), .en(en));
  Multiplexer multiplexer_11 (.in0(a2), .in1(multiplexer_3_out), .out(multiplexer_11_out), .sel(in_14), .en(en));
  Multiplexer multiplexer_12 (.in0(a3), .in1(multiplexer_4_out), .out(multiplexer_12_out), .sel(in_14), .en(en));
  Multiplexer multiplexer_13 (.in0(a4), .in1(multiplexer_5_out), .out(multiplexer_13_out), .sel(in_14), .en(en));
  Multiplexer multiplexer_14 (.in0(a5), .in1(multiplexer_6_out), .out(multiplexer_14_out), .sel(in_14), .en(en));
  Multiplexer multiplexer_15 (.in0(a6), .in1(multiplexer_7_out), .out(multiplexer_15_out), .sel(in_14), .en(en));
  Multiplexer multiplexer_16 (.in0(a7), .in1(multiplexer_8_out), .out(multiplexer_16_out), .sel(in_14), .en(en));
  Multiplexer multiplexer_17 (.in0(_0), .in1(multiplexer_11_out), .out(multiplexer_17_out), .sel(not_2_out), .en(en));
  Multiplexer multiplexer_18 (
    .in0(multiplexer_9_out), .in1(multiplexer_12_out), .out(multiplexer_18_out), .sel(not_2_out), .en(en));
  Multiplexer multiplexer_19 (
    .in0(multiplexer_10_out), .in1(multiplexer_13_out), .out(multiplexer_19_out), .sel(not_2_out), .en(en));
  Multiplexer multiplexer_20 (
    .in0(multiplexer_11_out), .in1(multiplexer_14_out), .out(multiplexer_20_out), .sel(not_2_out), .en(en));
  Multiplexer multiplexer_21 (
    .in0(multiplexer_12_out), .in1(multiplexer_15_out), .out(multiplexer_21_out), .sel(not_2_out), .en(en));
  Multiplexer multiplexer_22 (
    .in0(multiplexer_13_out), .in1(multiplexer_16_out), .out(multiplexer_22_out), .sel(not_2_out), .en(en));
  Multiplexer multiplexer_23 (
    .in0(multiplexer_14_out), .in1(and_1_out), .out(multiplexer_23_out), .sel(not_2_out), .en(en));
  Multiplexer multiplexer_24 (
    .in0(multiplexer_15_out), .in1(and_1_out), .out(multiplexer_24_out), .sel(not_2_out), .en(en));
  Multiplexer multiplexer_25 (
    .in0(multiplexer_9_out), .in1(multiplexer_17_out), .out(multiplexer_25_out), .sel(in_15), .en(en));
  Multiplexer multiplexer_26 (
    .in0(multiplexer_10_out), .in1(multiplexer_18_out), .out(multiplexer_26_out), .sel(in_15), .en(en));
  Multiplexer multiplexer_27 (
    .in0(multiplexer_11_out), .in1(multiplexer_19_out), .out(multiplexer_27_out), .sel(in_15), .en(en));
  Multiplexer multiplexer_28 (
    .in0(multiplexer_12_out), .in1(multiplexer_20_out), .out(multiplexer_28_out), .sel(in_15), .en(en));
  Multiplexer multiplexer_29 (
    .in0(multiplexer_13_out), .in1(multiplexer_21_out), .out(multiplexer_29_out), .sel(in_15), .en(en));
  Multiplexer multiplexer_30 (
    .in0(multiplexer_14_out), .in1(multiplexer_22_out), .out(multiplexer_30_out), .sel(in_15), .en(en));
  Multiplexer multiplexer_31 (
    .in0(multiplexer_15_out), .in1(multiplexer_23_out), .out(multiplexer_31_out), .sel(in_15), .en(en));
  Multiplexer multiplexer_32 (
    .in0(multiplexer_16_out), .in1(multiplexer_24_out), .out(multiplexer_32_out), .sel(in_15), .en(en));
  Multiplexer multiplexer_33 (.in0(_0), .in1(multiplexer_29_out), .out(multiplexer_33_out), .sel(not_2_out), .en(en));
  Multiplexer multiplexer_34 (.in0(_0), .in1(multiplexer_30_out), .out(multiplexer_34_out), .sel(not_2_out), .en(en));
  Multiplexer multiplexer_35 (.in0(_0), .in1(multiplexer_31_out), .out(multiplexer_35_out), .sel(not_2_out), .en(en));
  Multiplexer multiplexer_36 (.in0(_0), .in1(multiplexer_32_out), .out(multiplexer_36_out), .sel(not_2_out), .en(en));
  Multiplexer multiplexer_37 (
    .in0(multiplexer_25_out), .in1(and_1_out), .out(multiplexer_37_out), .sel(not_2_out), .en(en));
  Multiplexer multiplexer_38 (
    .in0(multiplexer_26_out), .in1(and_1_out), .out(multiplexer_38_out), .sel(not_2_out), .en(en));
  Multiplexer multiplexer_39 (
    .in0(multiplexer_27_out), .in1(and_1_out), .out(multiplexer_39_out), .sel(not_2_out), .en(en));
  Multiplexer multiplexer_40 (
    .in0(multiplexer_28_out), .in1(and_1_out), .out(multiplexer_40_out), .sel(not_2_out), .en(en));
  Multiplexer multiplexer_41 (.in0(multiplexer_25_out), .in1(multiplexer_33_out), .out(out_16), .sel(in_13), .en(en));
  Multiplexer multiplexer_42 (.in0(multiplexer_26_out), .in1(multiplexer_34_out), .out(out_17), .sel(in_13), .en(en));
  Multiplexer multiplexer_43 (.in0(multiplexer_27_out), .in1(multiplexer_35_out), .out(out_18), .sel(in_13), .en(en));
  Multiplexer multiplexer_44 (.in0(multiplexer_28_out), .in1(multiplexer_36_out), .out(out_19), .sel(in_13), .en(en));
  Multiplexer multiplexer_45 (.in0(multiplexer_29_out), .in1(multiplexer_37_out), .out(out_20), .sel(in_13), .en(en));
  Multiplexer multiplexer_46 (.in0(multiplexer_30_out), .in1(multiplexer_38_out), .out(out_21), .sel(in_13), .en(en));
  Multiplexer multiplexer_47 (.in0(multiplexer_31_out), .in1(multiplexer_39_out), .out(out_22), .sel(in_13), .en(en));
  Multiplexer multiplexer_48 (.in0(multiplexer_32_out), .in1(multiplexer_40_out), .out(out_23), .sel(in_13), .en(en));
endmodule
