// Logisim project display7.circ as structural Verilog: 1 circuit, main circuit main
module main (
  input  in_1,
  input  in_2,
  input  in_3,
  input  in_4,
  output g,
  output f,
  output e,
  output d,
  output c,
  output b,
  output a
);

  wire and_1_out, and_2_out, and_4_out, and_5_out, and_6_out, and_7_out, and_8_out, and_10_out, not_1_out,
       not_2_out, not_3_out, not_4_out, not_5_out, not_6_out, not_7_out, not_8_out, not_9_out, not_10_out,
       not_11_out, not_12_out, not_13_out, not_14_out, not_15_out, not_16_out, not_17_out, not_18_out,
       not_19_out;

  and and_1 (and_1_out, not_1_out, not_4_out, not_3_out, not_6_out);
  not not_1 (not_1_out, in_1);
  or or_1 (g, and_1_out, and_2_out, and_8_out);
  and and_2 (and_2_out, not_1_out, not_4_out, not_3_out, not_2_out);
  not not_2 (not_2_out, not_6_out);
  not not_3 (not_3_out, in_3);
  not not_4 (not_4_out, in_2);
  or or_2 (f, and_2_out, c, and_4_out, and_8_out);
  and and_3 (c, not_1_out, not_4_out, not_5_out, not_6_out);
  not not_5 (not_5_out, not_3_out);
  not not_6 (not_6_out, in_4);
  or or_3 (e, and_2_out, and_4_out, and_6_out, and_5_out, and_8_out, and_10_out);
  and and_4 (and_4_out, not_1_out, not_4_out, not_7_out, not_8_out);
  not not_7 (not_7_out, not_3_out);
  not not_8 (not_8_out, not_6_out);
  or or_4 (d, and_2_out, and_6_out, and_8_out);
  and and_5 (and_5_out, not_1_out, not_10_out, not_3_out, not_13_out);
  and and_6 (and_6_out, not_1_out, not_9_out, not_3_out, not_6_out);
  not not_9 (not_9_out, not_4_out);
  not not_10 (not_10_out, not_4_out);
  and and_7 (and_7_out, not_1_out, not_11_out, not_12_out, not_6_out);
  not not_11 (not_11_out, not_4_out);
  not not_12 (not_12_out, not_3_out);
  not not_13 (not_13_out, not_6_out);
  or or_5 (b, and_5_out, and_7_out);
  and and_8 (and_8_out, not_1_out, not_14_out, not_17_out, not_15_out);
  not not_14 (not_14_out, not_4_out);
  not not_15 (not_15_out, not_6_out);
  not not_16 (not_16_out, not_1_out);
  not not_17 (not_17_out, not_3_out);
  or or_6 (a, and_2_out, and_6_out);
  // AND_Gate and_9 has open pins: in0=not_16_out, in1=not_4_out, in2=not_3_out, in3=not_6_out, out=open
  and and_10 (and_10_out, not_18_out, not_19_out, not_3_out, not_6_out);
  not not_18 (not_18_out, not_1_out);
  not not_19 (not_19_out, not_4_out);

  // Notes on the sheet:
  //   D3
  //   D2
  //   D1
  //   D0
endmodule
