// Logisim project encoder10-4_Pri.circ as structural Verilog: 1 circuit, main circuit main
module main (
  input  in_1,
  input  in_2,
  input  in_3,
  input  in_4,
  input  in_5,
  input  in_6,
  input  in_7,
  input  in_8,
  input  in_9,
  input  in_10,
  output D0,
  output D1,
  output D2,
  output D3
);

  wire and_1_out, and_2_out, and_3_out, and_4_out, and_5_out, and_6_out, and_7_out, and_8_out, and_9_out,
       and_10_out, and_11_out, and_12_out, and_13_out, and_14_out, and_15_out, not_1_out, not_2_out,
       not_3_out, not_4_out, not_5_out, not_6_out, not_7_out, not_8_out, not_9_out;

  and and_1 (and_1_out, not_1_out, in_2, in_4, in_6, in_8, in_10);
  and and_2 (and_2_out, not_3_out, in_4, in_6, in_8, in_10);
  or or_1 (D0, and_1_out, and_2_out, and_3_out, and_4_out, and_5_out);
  and and_3 (and_3_out, not_5_out, in_6, in_8, in_10);
  not not_1 (not_1_out, in_1);
  and and_4 (and_4_out, not_7_out, in_8, in_10);
  not not_2 (not_2_out, in_2);
  and and_5 (and_5_out, not_9_out, in_10);
  not not_3 (not_3_out, in_3);
  and and_6 (and_6_out, not_3_out, in_5, in_6, in_7, in_8, in_9, in_10);
  not not_4 (not_4_out, in_4);
  or or_2 (D1, and_6_out, and_7_out, and_8_out, and_9_out);
  and and_7 (and_7_out, not_4_out, in_5, in_6, in_7, in_8, in_9, in_10);
  and and_8 (and_8_out, not_7_out, in_9, in_10);
  not not_5 (not_5_out, in_5);
  and and_9 (and_9_out, not_8_out, in_9, in_10);
  not not_6 (not_6_out, in_6);
  not not_7 (not_7_out, in_7);
  and and_10 (and_10_out, not_3_out, in_7, in_8, in_9, in_10);
  or or_3 (D2, and_10_out, and_12_out, and_11_out, and_13_out);
  and and_11 (and_11_out, not_5_out, in_7, in_8, in_9, in_10);
  and and_12 (and_12_out, not_4_out, in_7, in_8, in_9, in_10);
  not not_8 (not_8_out, in_8);
  and and_13 (and_13_out, not_6_out, in_7, in_8, in_9, in_10);
  not not_9 (not_9_out, in_9);
  and and_14 (and_14_out, not_1_out, in_3, in_4, in_5, in_6, in_7, in_8, in_9, in_10);
  or or_4 (D3, and_14_out, and_15_out);
  and and_15 (and_15_out, not_2_out, in_3, in_4, in_5, in_6, in_7, in_8, in_9, in_10);

  // Notes on the sheet:
  //   ~I9
  //   ~I8
  //   ~I7
  //   ~I6
  //   ~I5
  //   ~I4
  //   ~I3
  //   ~I2
  //   ~I1
  //   ~I0
endmodule
