// Logisim project encoder83_Pri.circ as structural Verilog: 1 circuit, main circuit main
module main (
  input  in_1,
  input  in_2,
  input  in_3,
  input  in_4,
  input  in_5,
  input  in_6,
  input  in_7,
  input  in_8,
  input  in_9,
  output nD0,
  output nD0_2,
  output nD1,
  output nD2
);

  wire and_1_out, and_2_out, and_3_out, and_4_out, and_5_out, and_6_out, and_7_out, and_8_out, and_9_out,
       and_10_out, and_11_out, and_12_out, not_2_out, not_3_out, not_4_out, not_5_out, not_6_out, not_7_out,
       not_8_out;

  not not_1 (nD0, in_1);
  and and_1 (and_1_out, not_2_out, in_4, in_6, in_8, nD0);
  nor nor_1 (nD0_2, and_1_out, and_2_out, and_4_out, and_3_out);
  and and_2 (and_2_out, not_4_out, in_6, in_8, nD0);
  not not_2 (not_2_out, in_3);
  and and_3 (and_3_out, not_8_out, nD0);
  and and_4 (and_4_out, not_6_out, in_8, nD0);
  and and_5 (and_5_out, not_3_out, in_6, in_7, nD0);
  not not_3 (not_3_out, in_4);
  nor nor_2 (nD1, and_5_out, and_6_out, and_7_out, and_8_out);
  and and_6 (and_6_out, not_4_out, in_6, in_7, nD0);
  not not_4 (not_4_out, in_5);
  and and_7 (and_7_out, not_7_out, nD0);
  and and_8 (and_8_out, not_8_out, nD0);
  not not_5 (not_5_out, in_6);
  and and_9 (and_9_out, not_5_out, nD0);
  nor nor_3 (nD2, and_9_out, and_10_out, and_12_out, and_11_out);
  and and_10 (and_10_out, not_6_out, nD0);
  not not_6 (not_6_out, in_7);
  and and_11 (and_11_out, not_8_out, nD0);
  and and_12 (and_12_out, not_7_out, nD0);
  not not_7 (not_7_out, in_8);
  not not_8 (not_8_out, in_9);

  // Notes on the sheet:
  //   !D0
  //   !D1
  //   !D2
  //   !D3
  //   !D4
  //   !D5
  //   !D6
  //   !D7
endmodule
