// Logisim project 计数器型_加法器.circ as structural Verilog: 1 circuit, main circuit main
module main (
  input  [7:0] in_1,
  output out_2,
  output [7:0] out_3
);

  wire A, ADD, and_1_out, and_2_out, and_3_out, and_5_out, and_6_out, B, CLR, LDA, LDB, not_2_out, not_3_out,
       not_4_out, not_5_out, not_6_out, or_1_out, or_2_out, OverFlow, T1, T2;
  wire [7:0] controlled_buffer_1_out, register_2_q, register_3_q;

  Clock clock_1 (.out(T1));
  not not_1 (T2, T1);
  Register #(.width(1)) register_1 (.D(OverFlow), .Q(out_2), .clk(and_1_out), .clr(CLR));  // open: en
  and and_1 (and_1_out, ADD, T2);
  or or_1 (or_1_out, A, B);
  Register register_2 (.D(in_1), .Q(register_2_q), .clk(and_2_out), .clr(CLR));  // open: en
  and and_2 (and_2_out, LDA, T2);
  D_Flip_Flop d_ff_1 (.clk(T1), .D(or_1_out), .Q(B));  // open: Qn, preset, en, reset
  assign controlled_buffer_1_out = ADD ? register_3_q : 8'bz;  // Controlled_Buffer controlled_buffer_1
  or or_2 (or_2_out, not_2_out, not_3_out);
  not not_2 (not_2_out, A);
  not not_3 (not_3_out, B);
  Adder adder_1 (.a(register_2_q), .b(controlled_buffer_1_out), .out(out_3), .cout(OverFlow));  // open: cin
  D_Flip_Flop d_ff_2 (.clk(T1), .D(or_2_out), .Q(A));  // open: Qn, preset, en, reset
  Register register_3 (.D(out_3), .Q(register_3_q), .clk(and_3_out), .clr(CLR));  // open: en
  and and_3 (and_3_out, T2, LDB);
  and and_4 (ADD, not_4_out, B);
  not not_4 (not_4_out, A);
  or or_3 (LDA, and_5_out, and_6_out);
  and and_5 (and_5_out, not_6_out, not_5_out);
  not not_5 (not_5_out, B);
  not not_6 (not_6_out, A);
  and and_6 (and_6_out, A, B);
  nor nor_1 (CLR, A, B);
  xor xor_1 (LDB, A, B);
endmodule
