// Logisim project 计数器型加法器.circ as structural Verilog: 1 circuit, main circuit main
module main (
  input  [7:0] in_1,
  output out_2,
  output [7:0] out_3
);

  wire A, ADD, and_1_out, and_2_out, and_3_out, B, CLR, LDA, LDB, nand_1_out, not_2_out, or_1_out, OVERFLOW,
       T1, T2;
  wire [7:0] controlled_buffer_1_out, register_2_q, register_3_q;

  Clock clock_1 (.out(T1));
  not not_1 (T2, T1);
  Register #(.width(1)) register_1 (.D(OVERFLOW), .Q(out_2), .clk(and_1_out), .clr(CLR));  // open: en
  and and_1 (and_1_out, ADD, T2);
  or or_1 (or_1_out, A, B);
  Register register_2 (.D(in_1), .Q(register_2_q), .clk(and_2_out), .clr(CLR));  // open: en
  and and_2 (and_2_out, T2, LDA);
  D_Flip_Flop d_ff_1 (.clk(T1), .D(or_1_out), .Q(A));  // open: Qn, preset, en, reset
  assign controlled_buffer_1_out = ADD ? register_3_q : 8'bz;  // Controlled_Buffer controlled_buffer_1
  Adder adder_1 (.a(register_2_q), .b(controlled_buffer_1_out), .out(out_3), .cout(OVERFLOW));  // open: cin
  Register register_3 (.D(out_3), .Q(register_3_q), .clk(and_3_out), .clr(CLR));  // open: en
  and and_3 (and_3_out, T2, LDB);
  nand nand_1 (nand_1_out, A, B);
  D_Flip_Flop d_ff_2 (.clk(T1), .D(nand_1_out), .Q(B));  // open: Qn, preset, en, reset
  not not_2 (not_2_out, A);
  nor nor_1 (CLR, A, B);
  xnor xnor_1 (LDA, A, B);
  xor xor_1 (LDB, A, B);
  and and_4 (ADD, not_2_out, B);
endmodule
