// Logisim project 计数器型比较器.circ as structural Verilog: 1 circuit, main circuit main
module main (
  input  [7:0] in_1,
  output out_2
);

  wire A, and_1_out, and_2_out, B, CAP, clock_1_out, CLR, LDA, LDB, not_1_out, not_2_out, not_4_out,
       or_1_out, or_2_out, xor_1_out;
  wire [7:0] controlled_buffer_1_out, controlled_buffer_2_out, register_1_q, register_2_q;

  Clock clock_1 (.out(clock_1_out));
  or or_1 (or_1_out, xor_1_out, and_1_out);
  xor xor_1 (xor_1_out, A, B);
  Register register_1 (.D(in_1), .Q(register_1_q), .clk(LDB), .clr(CLR));  // open: en
  D_Flip_Flop d_ff_1 (.clk(clock_1_out), .D(or_1_out), .Q(A));  // open: Qn, preset, en, reset
  and and_1 (and_1_out, B, out_2);
  Register register_2 (.D(register_1_q), .Q(register_2_q), .clk(LDA), .clr(CLR));  // open: en
  or or_2 (or_2_out, not_1_out, and_2_out);
  not not_1 (not_1_out, A);
  assign controlled_buffer_1_out = CAP ? register_2_q : 8'bz;  // Controlled_Buffer controlled_buffer_1
  assign controlled_buffer_2_out = CAP ? register_1_q : 8'bz;  // Controlled_Buffer controlled_buffer_2
  D_Flip_Flop d_ff_2 (.clk(clock_1_out), .D(or_2_out), .Q(B));  // open: Qn, preset, en, reset
  and and_2 (and_2_out, B, not_2_out);
  not not_2 (not_2_out, out_2);
  Comparator comparator_1 (.a(controlled_buffer_1_out), .b(controlled_buffer_2_out), .gt(out_2));  // open: eq, lt
  not not_3 (LDB, A);
  not not_4 (not_4_out, B);
  and and_3 (LDA, not_4_out, A);
  and and_4 (CLR, not_4_out, LDB);
  and and_5 (CAP, A, B);

  // Other names for the same wires on the sheet: A_B = out_2
endmodule
